# Fritzing sketch Battery-ESP-ds18b20 (saved by Fritzing 0.9.2b)

parts:
  DS1 = DS18B20 1-Wire Temperature Sensor [part_number=DS18B20]
  R1 = Resistor [tolerance=±5% resistance=4.7k package=THT]
  VCC1 = 4 x AAA Battery Mount
  U1 = NodeMCU V1.0

nets:
  GND: DS1.GND, VCC1.-, U1.GND
  N1: DS1.DQ, R1.Pin_1, U1.D5
  VDD: DS1.VDD, R1.Pin_0, U1.3V3
  N2: VCC1.+, U1.Vin
  N3: U1.D0, U1.RST

notes:
  4,7 KΩ
  4x Ni-MH 1.2 rechargable batteries
  or
  5V USB power
  cyan wire = reset wire for deep sleep

custom parts:
  NodeMCU V1.0: ESP9266 based NodeMCU
