# Fritzing sketch ESP-DHT (saved by Fritzing 0.9.2b)

parts:
  U1 = NodeMCU V1.0
  RHT1 = Humidity and Temperature Sensor RHT03

nets:
  N1: U1.D4, RHT1.Data-signal
  3V3: U1.3V3, RHT1.Vcc
  N2: U1.GND, RHT1.GND_2

custom parts:
  NodeMCU V1.0: ESP9266 based NodeMCU
