# Fritzing sketch ESP-ds18b20 (saved by Fritzing 0.9.2b)

parts:
  DS1 = DS18B20 1-Wire Temperature Sensor [part_number=DS18B20]
  R1 = Resistor [tolerance=±5% resistance=4.7k package=THT]
  U1 = NodeMCU V1.0

nets:
  GND: DS1.GND, U1.GND
  N1: DS1.DQ, R1.Pin_1, U1.D5
  VDD: DS1.VDD, R1.Pin_0, U1.3V3

notes:
  4,7 KΩ

custom parts:
  NodeMCU V1.0: ESP9266 based NodeMCU
