# Fritzing sketch ESP-relay (saved by Fritzing 0.9.2b)

parts:
  U1 = NodeMCU V1.0
  KY-1 = Keyes Relay [package=THT]

nets:
  N1: U1.D4, KY-1.signal
  N2: U1.3V3, KY-1.power
  N3: U1.GND, KY-1.ground

notes:
  Relay Pin layouts can differ:
  [Relay] [ESP]
  Vcc 3.3V or 5V (Vin)
  GND GND
  In1 D4 (aka GPIO2 aka TXD1)

custom parts:
  NodeMCU V1.0: ESP9266 based NodeMCU
  Keyes Relay: The Keyes 5V relay module is suitable for SCM development, home appliance control. It uses a 5V~12V TIL control signal which can control DC / AC signal.
