# Fritzing sketch RF-ds18b20-LP-NoBreadboard (saved by Fritzing 0.9.2b)

parts:
  Onderdeel1 = Arduino Nano (Rev3.0) (ICSP)
  DS1 = DS18B20 1-Wire Temperature Sensor [part_number=DS18B20]
  R1 = Resistor [tolerance=±5% resistance=4.7k package=THT]
  VCC1 = 4 x AAA Battery Mount  # not connected
  R2 = Resistor [tolerance=±5% resistance=1M package=THT]
  R3 = Resistor [tolerance=±5% resistance=470k package=THT]  # not connected
  U1 = RF-LINK_TX [package=rf-link_tx]

nets:
  GND: Onderdeel1.GND, U1.GND
  N1: Onderdeel1.D4, U1.DATA
  N2: Onderdeel1.D5, DS1.DQ, R1.Pin_1
  N3: Onderdeel1.A0, R2.Pin_1
  N4: DS1.VDD, R1.Pin_0
  N5: R2.Pin_0, U1.+5V

notes:
  RF-433 TX
  1 MΩ
  470 KΩ
  4,7 KΩ
  4x Ni-MH 1.2 rechargable batteries
  dupont wire cut to 17cm as antenna
